# Fritzing sketch schematic (saved by Fritzing 0.9.3b)
breadboards: 1

parts:
  Part1 = Arduino Nano (Rev3.0)
  DC-DC_Converter = IC, DIP package, 4 pins [chip_label=MT3608]
  Power_switch = SWITCH-SPST-2 [package=switch-spst-vertical]
  Battery_18650 = Battery Holders [package=battery-aa-kit]
  X1 = USB Connectors [package=usb-a-s]
  CO2_Sensor = IC, DIP package, 4 pins [chip_label=MH-Z14B]
  Battery_charge_and_protection = IC, DIP package, 6 pins [chip_label=TP4056]
  Oled_screen = IC, DIP package, 4 pins [chip_label=SSD1306]

nets:
  GND: Part1.GND, DC-DC_Converter.pin3, CO2_Sensor.pin4, Oled_screen.pin4
  N1: Part1.D2, CO2_Sensor.pin3
  N2: Part1.D4, CO2_Sensor.pin2
  5V: Part1.5V, DC-DC_Converter.pin4, CO2_Sensor.pin1, Oled_screen.pin1
  N3: Part1.A5, Oled_screen.pin2
  N4: Part1.A4, Oled_screen.pin3
  N5: DC-DC_Converter.pin1, Battery_charge_and_protection.pin6
  N6: DC-DC_Converter.pin2, Power_switch.O
  N7: Power_switch.P, Battery_charge_and_protection.pin5
  N8: Battery_18650.+, Battery_charge_and_protection.pin3
  N9: Battery_18650.-, Battery_charge_and_protection.pin4
  N10: X1.GND, Battery_charge_and_protection.pin1
  N11: X1.VBUS, Battery_charge_and_protection.pin2

notes:
  Portable CO2 Sensor, 1
